# Fritzing sketch Electronics (saved by Fritzing 0.9.3b)

parts:
  Composant5 = Arduino Mega 2560 (Rev3)
  R7 = Slide Potentiometer [maximum_resistance=100kΩ]
  S26 = Pushbutton [package="[THT]"]
  R8 = Resistor [tolerance=±5% resistance=10k package=THT]
  R9 = Slide Potentiometer [maximum_resistance=100kΩ]
  Composant6 = Thumb Joystick
  Composant7 = Thumb Joystick
  Composant8 = Thumb Joystick
  S30 = Toggle Switch [package=THT]
  S31 = Toggle Switch [package=THT]
  S32 = Toggle Switch [package=THT]
  S33 = Toggle Switch [package=THT]
  S34 = Toggle Switch [package=THT]
  S35 = Toggle Switch [package=THT]
  S36 = Toggle Switch [package=THT]
  S37 = Toggle Switch [package=THT]
  S38 = Toggle Switch [package=THT]
  S39 = Toggle Switch [package=THT]
  S40 = Toggle Switch [package=THT]
  S41 = Toggle Switch [package=THT]
  S42 = Toggle Switch [package=THT]
  S43 = Toggle Switch [package=THT]
  S44 = Toggle Switch [package=THT]
  S45 = Toggle Switch [package=THT]
  S46 = Toggle Switch [package=THT]
  S47 = Toggle Switch [package=THT]
  LED24 = LED - 5mm [color="Red (633nm)" package="5 mm [THT]"]
  LED25 = LED - 5mm [color="Green (555nm)" package="5 mm [THT]"]
  LED28 = LED - 5mm [color="Red (633nm)" package="5 mm [THT]"]
  LED29 = LED - 5mm [color="White (4500K)" package="5 mm [THT]"]
  LED32 = LED - 5mm [color="Red (633nm)" package="5 mm [THT]"]
  LED33 = LED - 5mm [color="Yellow (595nm)" package="5 mm [THT]"]
  LED36 = LED - 5mm [color="Blue (430nm)" package="5 mm [THT]"]
  LED39 = LED - 5mm [color="Red (633nm)" package="5 mm [THT]"]
  S48 = Toggle Switch [package=THT]
  LED40 = LED - 5mm [color="Red (633nm)" package="5 mm [THT]"]

nets:
  N1: Composant5.A0, R7.wiper
  N2: Composant5.A1, R9.wiper
  N3: Composant5.A2, Composant6.HORZ
  N4: Composant5.A3, Composant6.VERT
  N5: Composant5.A4, Composant7.HORZ
  N6: Composant5.A5, Composant7.VERT
  N7: Composant5.A6, Composant8.HORZ
  N8: Composant5.A7, Composant8.VERT
  N9: Composant5.D20/SDA, S41.COM
  N10: Composant5.D18/TX1, S37.COM
  N11: Composant5.D16_PWM/TX2, S33.COM
  N12: Composant5.D13_PWM, S26.Pin_3
  N13: Composant5.D12_PWM, Composant6.SEL
  VCC: Composant5.5V, R7.leg1, S26.Pin_1, S26.Pin_2, R9.leg1, Composant6.VCC, Composant7.VCC, Composant8.VCC, S30.L1, S31.L1, S32.L1, S33.L1, S34.L1, S35.L1, S36.L1, S37.L1, S38.L1, S39.L1, S40.L1, S41.L1, S42.L1, S43.L1, S44.L1, S45.L1, S46.L1, S47.L1, LED24.anode, LED25.anode, LED28.anode, LED29.anode, LED32.anode, LED33.anode, LED36.cathode, LED39.cathode, S48.L1, LED40.anode
  GND: Composant5.GND, R7.leg2, R8.Pin_0, R9.leg2, Composant6.GND, Composant7.GND, Composant8.GND, S30.L2, S31.L2, S32.L2, S33.L2, S34.L2, S35.L2, S36.L2, S37.L2, S39.L2, S40.L2, S41.L2, S42.L2, S43.L2, S44.L2, S45.L2, S46.L2, S47.L2, S48.L2
  N14: Composant5.D22, S30.COM
  N15: Composant5.D23, LED25.cathode
  N16: Composant5.D24, S34.COM
  N17: Composant5.D25, LED29.cathode
  N18: Composant5.D26, S38.COM
  N19: Composant5.D27, LED33.cathode
  N20: Composant5.D28, S42.COM
  N21: Composant5.D29, LED36.anode
  N22: Composant5.D30, S45.COM
  N23: Composant5.D31, LED39.anode
  N24: Composant5.D32, S31.COM
  N25: Composant5.D33, LED24.cathode
  N26: Composant5.D34, S35.COM
  N27: Composant5.D35, LED28.cathode
  N28: Composant5.D36, S39.COM
  N29: Composant5.D37, LED32.cathode
  N30: Composant5.D38, S48.COM
  N31: Composant5.D39, LED40.cathode
  N32: Composant5.D42, S36.COM
  N33: Composant5.D44, S40.COM
  N34: Composant5.D46, S43.COM
  N35: Composant5.D48, S46.COM
  N36: Composant5.D50, S44.COM
  N37: Composant5.D52, S47.COM

notes:
  Throttle
  Staging
  Zoom
  Vue
  Pitch and yaw (and roll ?)
  Translation
  Gears
  Light
  SAS
  RCS
  Brakes
  Grpe d'action 6
  Grpe d'action 7
  Grpe d'action 8
  Grpe d'action 9
  Grpe d'action 10
  Grpe d'action 5
  Grpe d'action 4
  Grpe d'action 3
  Grpe d'action 2
  Grpe d'action 1
  Solar pannels
  Antennas
  Thrust reversers
  Abort
