# Fritzing sketch Montage version 1 (saved by Fritzing 0.9.3b)

parts:
  Composant1 = Arduino Mega 2560 (Rev3)
  R1 = Slide Potentiometer [maximum_resistance=100kΩ]
  S1 = Pushbutton [package="[THT]"]
  R2 = Resistor [tolerance=±5% resistance=10k package=THT]
  R3 = Slide Potentiometer [maximum_resistance=100kΩ]
  Composant2 = Thumb Joystick
  Composant3 = Thumb Joystick
  Composant4 = Thumb Joystick
  S2 = Pushbutton [package="[THT]"]
  S3 = Pushbutton [package="[THT]"]
  S4 = Pushbutton [package="[THT]"]
  R4 = Resistor [tolerance=±5% resistance=10k package=THT]
  R5 = Resistor [tolerance=±5% resistance=10k package=THT]
  R6 = Resistor [tolerance=±5% resistance=10k package=THT]
  S5 = Toggle Switch [package=THT]
  S6 = Toggle Switch [package=THT]
  S7 = Toggle Switch [package=THT]
  S8 = Toggle Switch [package=THT]
  S9 = Toggle Switch [package=THT]
  S10 = Toggle Switch [package=THT]
  S11 = Toggle Switch [package=THT]
  S12 = Toggle Switch [package=THT]
  S13 = Toggle Switch [package=THT]
  S14 = Toggle Switch [package=THT]
  S15 = Toggle Switch [package=THT]
  S16 = Toggle Switch [package=THT]
  S17 = Toggle Switch [package=THT]
  S20 = Toggle Switch [package=THT]
  S21 = Toggle Switch [package=THT]
  S22 = Toggle Switch [package=THT]
  S23 = Toggle Switch [package=THT]
  S24 = Toggle Switch [package=THT]
  LED1 = LED - 5mm [color="Green (555nm)" package="5 mm [THT]"]
  LED2 = LED - 5mm [color="White (4500K)" package="5 mm [THT]"]
  LED3 = LED - 5mm [color="Yellow (595nm)" package="5 mm [THT]"]
  LED4 = LED - 5mm [color="Blue (430nm)" package="5 mm [THT]"]
  LED5 = LED - 5mm [color="Red (633nm)" package="5 mm [THT]"]
  LED6 = LED - 5mm [color="Red (633nm)" package="5 mm [THT]"]
  LED7 = LED - 5mm [color="Red (633nm)" package="5 mm [THT]"]
  LED8 = LED - 5mm [color="Red (633nm)" package="5 mm [THT]"]
  LED11 = LED - 5mm [color="Blue (430nm)" package="5 mm [THT]"]
  LED12 = LED - 5mm [color="Blue (430nm)" package="5 mm [THT]"]
  LED13 = LED - 5mm [color="Blue (430nm)" package="5 mm [THT]"]
  LED14 = LED - 5mm [color="Blue (430nm)" package="5 mm [THT]"]
  LED15 = LED - 5mm [color="Blue (430nm)" package="5 mm [THT]"]
  LED16 = LED - 5mm [color="Blue (430nm)" package="5 mm [THT]"]
  LED17 = LED - 5mm [color="Blue (430nm)" package="5 mm [THT]"]
  LED18 = LED - 5mm [color="Blue (430nm)" package="5 mm [THT]"]
  LED19 = LED - 5mm [color="Blue (430nm)" package="5 mm [THT]"]
  LED20 = LED - 5mm [color="Blue (430nm)" package="5 mm [THT]"]
  S25 = Toggle Switch [package=THT]
  LED21 = LED - 5mm [color="Red (633nm)" package="5 mm [THT]"]
  RE1 = Rotary Encoder [package=THT]
  RE2 = Rotary Encoder [package=THT]
  RE3 = Rotary Encoder [package=THT]

nets:
  N1: Composant1.A0, R1.wiper
  N2: Composant1.A1, R3.wiper
  N3: Composant1.A2, Composant2.HORZ
  N4: Composant1.A3, Composant2.VERT
  N5: Composant1.A4, Composant3.HORZ
  N6: Composant1.A5, Composant3.VERT
  N7: Composant1.A6, Composant4.HORZ
  N8: Composant1.A7, Composant4.VERT
  N9: Composant1.D21/SCL, LED18.cathode
  N10: Composant1.D20/SDA, S7.COM
  N11: Composant1.D19/RX1, LED17.cathode
  N12: Composant1.D18/TX1, S6.COM
  N13: Composant1.D17_PWM/RX2, LED16.cathode
  N14: Composant1.D16_PWM/TX2, S5.COM
  GND: Composant1.GND, R1.leg2, R2.Pin_0, R3.leg2, Composant2.GND, Composant3.GND, Composant4.GND, R4.Pin_1, R5.Pin_1, R6.Pin_1, S5.L2, S6.L2, S7.L2, S8.L2, S9.L2, S10.L2, S11.L2, S12.L2, S13.L2, S14.L2, S15.L2, S16.L2, S17.L2, S20.L2, S21.L2, S23.L2, S24.L2, S25.L2
  N15: Composant1.D13_PWM, S1.Pin_3
  N16: Composant1.D12_PWM, Composant2.SEL
  N17: Composant1.D11_PWM, S2.Pin_3, S2.Pin_4
  N18: Composant1.D10_PWM, S3.Pin_3, S3.Pin_4
  N19: Composant1.D9_PWM, S4.Pin_4
  N20: Composant1.D8_PWM, RE1.EncoderPinA
  VCC: Composant1.5V, R1.leg1, S1.Pin_1, S1.Pin_2, R3.leg1, Composant2.VCC, Composant3.VCC, Composant4.VCC, S2.Pin_1, S2.Pin_2, S3.Pin_1, S3.Pin_2, S4.Pin_1, S4.Pin_2, S5.L1, S6.L1, S7.L1, S8.L1, S9.L1, S10.L1, S11.L1, S12.L1, S13.L1, S14.L1, S15.L1, S16.L1, S17.L1, S20.L1, S21.L1, S22.L1, S23.L1, S24.L1, LED1.anode, LED2.anode, LED3.anode, LED4.cathode, LED5.cathode, LED6.anode, LED7.anode, LED8.anode, LED11.anode, LED12.anode, LED13.anode, LED14.anode, LED15.anode, LED16.anode, LED17.anode, LED18.anode, LED19.anode, LED20.anode, S25.L1, LED21.anode
  N21: Composant1.D3_PWM, RE3.EncoderPinC
  N22: Composant1.D4_PWM, RE3.EncoderPinA
  N23: Composant1.D5_PWM, RE2.EncoderPinC
  N24: Composant1.D6_PWM, RE2.EncoderPinA
  N25: Composant1.D7_PWM, RE1.EncoderPinC
  N26: Composant1.D22, S20.COM
  N27: Composant1.D23, LED1.cathode
  N28: Composant1.D24, S21.COM
  N29: Composant1.D25, LED2.cathode
  N30: Composant1.D26, S22.COM
  N31: Composant1.D27, LED3.cathode
  N32: Composant1.D28, S23.COM
  N33: Composant1.D29, LED4.anode
  N34: Composant1.D30, S24.COM
  N35: Composant1.D31, LED5.anode
  N36: Composant1.D32, S15.COM
  N37: Composant1.D33, LED6.cathode
  N38: Composant1.D34, S16.COM
  N39: Composant1.D35, LED7.cathode
  N40: Composant1.D36, S17.COM
  N41: Composant1.D37, LED8.cathode
  N42: Composant1.D38, S25.COM
  N43: Composant1.D39, LED21.cathode
  N44: Composant1.D41, LED11.cathode
  N45: Composant1.D42, S11.COM
  N46: Composant1.D43, LED12.cathode
  N47: Composant1.D44, S12.COM
  N48: Composant1.D45, LED13.cathode
  N49: Composant1.D46, S13.COM
  N50: Composant1.D47, LED14.cathode
  N51: Composant1.D48, S14.COM, LED15.cathode
  N52: Composant1.D50, S8.COM
  N53: Composant1.D51, LED19.cathode
  N54: Composant1.D52, S9.COM
  N55: Composant1.D53, LED20.cathode

notes:
  Throttle
  Staging
  Zoom
  Vue
  Pitch and yaw (and roll ?)
  Translation
  Controle d'écran
  Gears
  Light
  SAS
  RCS
  Brakes
  Grpe d'action 1
  Grpe d'action 2
  Grpe d'action 3
  Grpe d'action 4
  Grpe d'action 5
  Grpe d'action 10
  Grpe d'action 9
  Grpe d'action 8
  Grpe d'action 7
  Grpe d'action 6
  Solar pannels
  Antennas
  Thrust reversers
  Abort
  Autopilot
